# Fritzing sketch LED-PWM-Fade-to-RPi-Pico-W (saved by Fritzing 0.8.7b)
breadboards: 1

parts:
  Mod2 = Raspberry Pi Pico W
  LED1 = LED - 5mm [color="Yellow (585nm)" package="5 mm [THT]"]
  R1 = Resistor [tolerance=±5% resistance=220 package=THT]

nets:
  N1: Mod2.pin_3, Mod2.pin_8, Mod2.pin_13, Mod2.pin_18, Mod2.pin_23, Mod2.pin_28, Mod2.pin_33, Mod2.pin_38, R1.Pin_1
  N2: Mod2.pin_20, LED1.anode
  N3: LED1.cathode, R1.Pin_0

custom parts:
  Raspberry Pi Pico W: Raspberry Pi Pico W. Based around the RP2040 microcontroller the Pico W is a low cost microcontroller device bringing Raspberry Pi quality, cost, and easy of use to the microcontroller space. The areas marked KEEPOUT in pcb silkscreen should not have traces running through them to avoid shorts on a soldered in module!
