# Fritzing sketch Active-Buzzer-to-RPi-Pico-W (saved by Fritzing 0.8.7b)
breadboards: 1

parts:
  Mod2 = Raspberry Pi Pico W
  Mod3 = KY-012 Active Buzzer Module [package="Breakout board"]

nets:
  N1: Mod2.pin_3, Mod2.pin_8, Mod2.pin_13, Mod2.pin_18, Mod2.pin_23, Mod2.pin_28, Mod2.pin_33, Mod2.pin_38, Mod3.-
  N2: Mod2.pin_20, Mod3.S

custom parts:
  Raspberry Pi Pico W: Raspberry Pi Pico W. Based around the RP2040 microcontroller the Pico W is a low cost microcontroller device bringing Raspberry Pi quality, cost, and easy of use to the microcontroller space. The areas marked KEEPOUT in pcb silkscreen should not have traces running through them to avoid shorts on a soldered in module!
  KY-012 Active Buzzer Module: Active Piezoelectric Buzzer Module KY-012, it produces single-tone sound when signal is high. (Special thanks to vanepp for fixing the PCB holes and other errors)
