# Fritzing sketch LCD-I2C-to-RPi-Pico-W (saved by Fritzing 0.8.7b)
breadboards: 1

parts:
  Mod2 = Raspberry Pi Pico W
  Part1 = LCD1602-I2C

nets:
  N1: Mod2.pin_1, Part1.SDA
  N2: Mod2.pin_2, Part1.SCL
  N3: Mod2.pin_3, Mod2.pin_8, Mod2.pin_13, Mod2.pin_18, Mod2.pin_23, Mod2.pin_28, Mod2.pin_33, Mod2.pin_38, Part1.GND
  N4: Mod2.pin_40, Part1.VCC

custom parts:
  Raspberry Pi Pico W: Raspberry Pi Pico W. Based around the RP2040 microcontroller the Pico W is a low cost microcontroller device bringing Raspberry Pi quality, cost, and easy of use to the microcontroller space. The areas marked KEEPOUT in pcb silkscreen should not have traces running through them to avoid shorts on a soldered in module!
  LCD1602-I2C: A standard character display, usually with 2x16 characters. Comes in many colors with LCM1602 IIC attached.
