# Fritzing sketch Liquid-Level-Sensor-to-RPi-Pico-W (saved by Fritzing 0.8.7b)
breadboards: 1

parts:
  Water_Level_Sensor1 = Water Level Sensor
  Mod3 = Raspberry Pi Pico W

nets:
  N1: Water_Level_Sensor1.SIG, Mod3.pin_34
  N2: Water_Level_Sensor1.VCC, Mod3.pin_36
  N3: Water_Level_Sensor1.GND, Mod3.pin_3, Mod3.pin_8, Mod3.pin_13, Mod3.pin_18, Mod3.pin_23, Mod3.pin_28, Mod3.pin_33, Mod3.pin_38

custom parts:
  Water Level Sensor: A water level sensor. This sensor operates at 3V to 5V. The Sig (signal) pin outputs an analogue signal that is in proportion to the amount of water in contact with the sensor.
  Raspberry Pi Pico W: Raspberry Pi Pico W. Based around the RP2040 microcontroller the Pico W is a low cost microcontroller device bringing Raspberry Pi quality, cost, and easy of use to the microcontroller space. The areas marked KEEPOUT in pcb silkscreen should not have traces running through them to avoid shorts on a soldered in module!
