# Fritzing sketch PIR-Sensor-to-RPi-Pico-W (saved by Fritzing 0.8.7b)
breadboards: 1

parts:
  Mod2 = Raspberry Pi Pico W
  PIR1 = PIR sensor

nets:
  N1: Mod2.pin_3, Mod2.pin_8, Mod2.pin_13, Mod2.pin_18, Mod2.pin_23, Mod2.pin_28, Mod2.pin_33, Mod2.pin_38, PIR1.GND
  N2: Mod2.pin_21, PIR1.SIG
  N3: Mod2.pin_36, PIR1.VDD

custom parts:
  Raspberry Pi Pico W: Raspberry Pi Pico W. Based around the RP2040 microcontroller the Pico W is a low cost microcontroller device bringing Raspberry Pi quality, cost, and easy of use to the microcontroller space. The areas marked KEEPOUT in pcb silkscreen should not have traces running through them to avoid shorts on a soldered in module!
